// Logisim project InfoIIUebung1.circ as structural Verilog
module NOT_Gatter (
  input  x1,
  output y1
);

  nand nand_1 (y1, x1, 1'b1);
endmodule

module AND_Gatter (
  input  x1,
  input  x2,
  output y1
);

  wire nand_1_out, nand_2_out;

  nand nand_1 (nand_1_out, x1, x2);
  nand nand_2 (nand_2_out, x1, x2);
  nand nand_3 (y1, nand_1_out, nand_2_out);
endmodule

module OR_Gatter (
  input  x1,
  input  x2,
  output y1
);

  wire nand_1_out, nand_2_out;

  nand nand_1 (nand_1_out, x1, x1);
  nand nand_2 (nand_2_out, x2, x2);
  nand nand_3 (y1, nand_1_out, nand_2_out);
endmodule

module MUX (
  input  e0,
  input  e1,
  input  s,
  output y
);

  wire and_1_out, and_2_out, not_1_out;

  not not_1 (not_1_out, s);
  and and_1 (and_1_out, e0, not_1_out);
  and and_2 (and_2_out, e1, s);
  or or_1 (y, and_1_out, and_2_out);
endmodule
